# Fritzing sketch pingpong_sensor (saved by Fritzing 0.9.2b)
breadboards: 1

parts:
  U1 = attiny85 [package=dip]
  J1 = Piezo Speaker
  SW-1 = Vibration sensor module
  R1 = Trimmer Potentiometer [maximum_resistance=10kΩ package=THT]
  X1 = USB Connectors [package=usb-a-pcb]
  LED1 = LED - 3mm [color="Red (633nm)" package="3 mm [THT]"]
  R2 = Resistor [tolerance=±5% resistance=220 package=THT]

nets:
  N1: U1.Pin_3, R1.leg1
  N2: U1.Pin_4, J1.pin1, SW-1.Ground, X1.D-, R2.Pin_1
  N3: U1.Pin_6, SW-1.Digital_output, LED1.anode
  N4: U1.Pin_8, SW-1.vcc, X1.D+
  N5: J1.pin2, R1.wiper
  N6: LED1.cathode, R2.Pin_0

custom parts:
  Vibration sensor module: Single-roller type full induction trigger switch. When no vibration or tilt, the product is ON conduction state, and in the steady state, when a vibration or tilt, the switch will be rendered instantly disconnect the conductive resistance increases, generating a current pulse signal, thereby triggering circuit. The default state of the swith is close Digital output Supply voltage:3.3V-5V On-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
